# Fritzing sketch Random Sound-Player (saved by Fritzing 0.9.3b)

parts:
  Bauteil1 = Arduino Uno (Rev3)
  Bauteil2 = MicroSD Card Module
  JACK1 = 2.1mm DC Barrel Jack
  SP1 = SPEAKER [package=pcb_mount_speaker]
  S1 = Momentary Switch [package=ksa_sealed_tac_switch]
  LED1 = LED - 5mm [color="Yellow (595nm)" package="5 mm [THT]"]
  VCC1 = 4 x AAA Battery Mount
  BUTTON1 = Waterproof Pushbutton (green)
  R1 = Resistor [tolerance=±5% resistance=120 package=THT]
  R2 = Resistor [tolerance=±10% resistance=10k package=THT]

nets:
  N1: Bauteil1.D9_PWM, SP1.+
  N2: Bauteil1.D10_PWM/SS, Bauteil2.CS
  N3: Bauteil1.D11_PWM/MOSI, Bauteil2.MOSI
  N4: Bauteil1.D12/MISO, Bauteil2.MISO
  N5: Bauteil1.D13/SCK, Bauteil2.SCK
  GND: Bauteil1.GND, Bauteil2.GND, SP1.-, LED1.cathode, R2.Pin_1
  N6: Bauteil1.D4, S1.4, R2.Pin_0
  5V: Bauteil1.5V, Bauteil2.VCC, S1.2, R1.Pin_0
  N7: JACK1.center, BUTTON1.no_name_yet#2, BUTTON1.no_name_yet#5
  N8: JACK1.sleeve, VCC1.-, BUTTON1.no_name_yet#4
  N9: LED1.anode, R1.Pin_1
  N10: VCC1.+, BUTTON1.no_name_yet#1

notes:
  [supposed to be Pushbutton with integrated LED]
  connectors:
  GND
  VCC
  MISO
  MOSI
  SCK
  CS

custom parts:
  2.1mm DC Barrel Jack: 2.1mm DC Barrel Jack with Thru-Hole Connectors (breadboardable)
  Waterproof Pushbutton (green): Waterproof Illuminated Pushbutton (green)
